// Logisim project offline1_v1.1.circ as structural Verilog: 1 circuit, main circuit main
module main (
  input  cs2,
  input  in_2,
  input  cs1,
  input  cs0,
  input  A3,
  input  A2,
  input  A1,
  input  A0,
  input  B3,
  input  B2,
  input  B1,
  input  B0,
  output Z,
  output C,
  output S,
  output V,
  output F3,
  output F2,
  output F1,
  output F0
);

  wire n7404_1_p2, n7404_1_p4, n7404_1_p6, n7404_1_p8, n7404_1_p10, n7404_1_p12, n7404_2_p5, n7404_2_p6,
       n7404_2_p7, n7404_2_p8, n7408_1__3__1y, n7408_1__6__2y, n7408_1__8__3y, n7408_1__11__4y,
       n7408_2__3__1y, n7408_2__6__2y, n7408_2__8__3y, n7408_2__11__4y, n7408_3_p3, n7408_3_p6,
       n7432_1__3__1y, n7432_1__6__2y, n7432_1__8__3y, n7432_1__11__4y, n7432_2__3__1y, n7432_2__6__2y,
       n7432_2__8__3y, n7432_2__11__4y, n7483_1__2__s3, n7483_1__6__s2, n7483_1__9__s1, n7483_1__14__cout,
       n7483_1__15__s4, n7486_1_p3, n7486_1_p6, n7486_1_p9, n7486_1_p12;

  // _7404 7404_1: pin names not known; wires that end beside it: cs0, n7404_1_p2, B3, n7404_1_p4, B2, n7404_1_p6, B1, n7404_1_p8, B0, n7404_1_p10, cs2, n7404_1_p12, n7404_1_p2
  _7408 u_7408_1 (
    ._1__1A(n7404_1_p2), ._2__1B(B3), ._3__1Y(n7408_1__3__1y), ._4__2A(n7404_1_p2), ._5__2B(B2),
    ._6__2Y(n7408_1__6__2y), ._13__4B(n7404_1_p2), ._12__4A(B1), ._11__4Y(n7408_1__11__4y),
    ._10__3B(n7404_1_p2), ._9__3A(B0), ._8__3Y(n7408_1__8__3y));  // open: _7__GND, _14__Vcc
  _7408 u_7408_2 (
    ._1__1A(cs0), ._2__1B(n7404_1_p4), ._3__1Y(n7408_2__3__1y), ._4__2A(cs0), ._5__2B(n7404_1_p6),
    ._6__2Y(n7408_2__6__2y), ._13__4B(cs0), ._12__4A(n7404_1_p10), ._11__4Y(n7408_2__11__4y), ._10__3B(cs0),
    ._9__3A(n7404_1_p8), ._8__3Y(n7408_2__8__3y));  // open: _7__GND, _14__Vcc
  _7432 u_7432_1 (
    ._1__1A(A3), ._2__1B(n7408_2__3__1y), ._3__1Y(n7432_1__3__1y), ._4__2A(A2), ._5__2B(n7408_2__6__2y),
    ._6__2Y(n7432_1__6__2y), ._13__4B(A1), ._12__4A(n7408_2__8__3y), ._11__4Y(n7432_1__11__4y), ._10__3B(A0),
    ._9__3A(n7408_2__11__4y), ._8__3Y(n7432_1__8__3y));  // open: _7__GND, _14__Vcc
  _7432 u_7432_2 (
    ._1__1A(n7404_1_p2), ._2__1B(n7404_1_p10), ._3__1Y(n7432_2__3__1y), ._4__2A(n7404_1_p2),
    ._5__2B(n7404_1_p8), ._6__2Y(n7432_2__6__2y), ._13__4B(n7404_1_p2), ._12__4A(n7404_1_p4),
    ._11__4Y(n7432_2__11__4y), ._10__3B(n7404_1_p2), ._9__3A(n7404_1_p6), ._8__3Y(n7432_2__8__3y));  // open: _7__GND, _14__Vcc
  _7483 u_7483_1 (
    ._1__A4(A3), ._2__S3(n7483_1__2__s3), ._3__A3(A2), ._4__B3(n7408_1__6__2y), ._6__S2(n7483_1__6__s2),
    ._7__B2(n7408_1__11__4y), ._8__A2(A1), ._16__B4(n7408_1__3__1y), ._15__S4(n7483_1__15__s4),
    ._14__Cout(n7483_1__14__cout), ._13__Cin(cs1), ._11__B1(n7408_1__8__3y), ._10__A1(A0),
    ._9__S1(n7483_1__9__s1));  // open: _5__Vcc, _12__GND
  // _7486 7486_1: pin names not known; wires that end beside it: n7432_1__8__3y, n7432_2__3__1y, n7486_1_p3, n7432_1__11__4y, n7432_2__6__2y, n7486_1_p6, n7432_2__11__4y, n7432_1__3__1y, n7486_1_p9, n7432_2__8__3y, n7432_1__6__2y, n7486_1_p12, n7486_1_p12, n7486_1_p6, n7486_1_p3
  // _74157 74157_1: pin names not known; wires that end beside it: cs2, n7483_1__9__s1, n7486_1_p3, F0, n7483_1__6__s2, n7486_1_p6, F1, in_2, n7483_1__15__s4, n7486_1_p9, F3, n7483_1__2__s3, n7486_1_p12, F2, n7483_1__15__s4, n7483_1__2__s3, n7483_1__6__s2, n7483_1__2__s3, n7483_1__9__s1
  // _7404 7404_2: pin names not known; wires that end beside it: n7432_2__11__4y, n7432_2__8__3y, n7432_2__6__2y, n7432_2__3__1y, n7404_2_p5, n7404_2_p6, n7404_2_p7, n7404_2_p8, F0, n7404_2_p5, F1, n7404_2_p6, F2, n7404_2_p7, F3, n7404_2_p8
  // _7408 7408_3: pin names not known; wires that end beside it: n7404_2_p8, n7404_2_p7, n7408_3_p3, n7404_2_p6, n7404_2_p5, n7408_3_p6, n7408_3_p3, n7408_3_p6, Z, n7483_1__14__cout, n7404_1_p12, C, n7408_3_p3, n7483_1__14__cout, V

  assign S = F3;

  // Notes on the sheet:
  //   XOR
  //   F3
  //   F2
  //   F1
  //   F0
  //   SUM
  //   F3
  //   F2
  //   F1
  //   F0
  //   FLAGS
endmodule
