// Logisim project offline1_v2.circ as structural Verilog: 1 circuit, main circuit main
module main (
  input  in_1,
  input  cs2,
  input  cs1,
  input  cs0,
  input  A3,
  input  A2,
  input  A1,
  input  A0,
  input  B3,
  input  B2,
  input  B1,
  input  B0,
  output Z,
  output C,
  output S,
  output V,
  output F3,
  output F2,
  output F1,
  output F0
);

  wire n7404_1__2__1y, n7404_1__4__2y, n7404_1__6__3y, n7404_1__8__4y, n7404_1__10__5y, n7404_1__12__6y,
       n7408_1__3__1y, n7408_1__6__2y, n7408_1__8__3y, n7408_1__11__4y, n7408_2__3__1y, n7408_2__6__2y,
       n7408_2__8__3y, n7408_2__11__4y, n7408_3__3__1y, n7408_3__6__2y, n7408_3__8__3y, n7408_3__11__4y,
       n7408_4__3__1y, n7408_4__6__2y, n7408_4__8__3y, n7408_4__11__4y, n7432_1__3__1y, n7432_1__6__2y,
       n7432_1__8__3y, n7432_1__11__4y, n7432_2__3__1y, n7432_2__6__2y, n7432_2__8__3y, n7432_2__11__4y,
       n7432_3_p2, n7432_3_p3, n7432_3_p4, n7483_2__14__cout, n7483_3__14__cout, n7483_4__14__cout;

  _7404 u_7404_1 (
    ._1__1A(B3), ._2__1Y(n7404_1__2__1y), ._3__2A(B2), ._4__2Y(n7404_1__4__2y), ._5__3A(B1),
    ._6__3Y(n7404_1__6__3y), ._7__GND(1'b0), ._14__Vcc(1'b1), ._13__6A(B0), ._12__6Y(n7404_1__12__6y),
    ._11__5A(cs2), ._10__5Y(n7404_1__10__5y), ._9__4A(cs0), ._8__4Y(n7404_1__8__4y));
  _7408 u_7408_1 (
    ._1__1A(cs0), ._2__1B(n7408_2__3__1y), ._3__1Y(n7408_1__3__1y), ._4__2A(cs0), ._5__2B(n7408_2__6__2y),
    ._6__2Y(n7408_1__6__2y), ._7__GND(1'b0), ._14__Vcc(1'b1), ._13__4B(cs0), ._12__4A(n7408_2__11__4y),
    ._11__4Y(n7408_1__11__4y), ._10__3B(cs0), ._9__3A(n7408_2__8__3y), ._8__3Y(n7408_1__8__3y));
  _7408 u_7408_2 (
    ._1__1A(cs2), ._2__1B(n7404_1__2__1y), ._3__1Y(n7408_2__3__1y), ._4__2A(cs2), ._5__2B(n7404_1__4__2y),
    ._6__2Y(n7408_2__6__2y), ._7__GND(1'b0), ._14__Vcc(1'b1), ._13__4B(cs2), ._12__4A(n7404_1__6__3y),
    ._11__4Y(n7408_2__11__4y), ._10__3B(cs2), ._9__3A(n7404_1__12__6y), ._8__3Y(n7408_2__8__3y));
  _7408 u_7408_3 (
    ._1__1A(n7404_1__8__4y), ._2__1B(B3), ._3__1Y(n7408_3__3__1y), ._4__2A(n7404_1__8__4y), ._5__2B(B2),
    ._6__2Y(n7408_3__6__2y), ._7__GND(1'b0), ._14__Vcc(1'b1), ._13__4B(n7404_1__8__4y), ._12__4A(B1),
    ._11__4Y(n7408_3__11__4y), ._10__3B(n7404_1__8__4y), ._9__3A(B0), ._8__3Y(n7408_3__8__3y));
  _7432 u_7432_1 (
    ._1__1A(A3), ._2__1B(n7408_1__3__1y), ._3__1Y(n7432_1__3__1y), ._4__2A(A2), ._5__2B(n7408_1__6__2y),
    ._6__2Y(n7432_1__6__2y), ._7__GND(1'b0), ._14__Vcc(1'b1), ._13__4B(A1), ._12__4A(n7408_1__11__4y),
    ._11__4Y(n7432_1__11__4y), ._10__3B(A0), ._9__3A(n7408_1__8__3y), ._8__3Y(n7432_1__8__3y));
  _7432 u_7432_2 (
    ._1__1A(n7408_2__3__1y), ._2__1B(n7408_3__3__1y), ._3__1Y(n7432_2__3__1y), ._4__2A(n7408_2__6__2y),
    ._5__2B(n7408_3__6__2y), ._6__2Y(n7432_2__6__2y), ._7__GND(1'b0), ._14__Vcc(1'b1),
    ._13__4B(n7408_2__11__4y), ._12__4A(n7408_3__11__4y), ._11__4Y(n7432_2__11__4y),
    ._10__3B(n7408_3__8__3y), ._9__3A(n7408_2__8__3y), ._8__3Y(n7432_2__8__3y));
  _7483 u_7483_1 (
    ._1__A4(n7432_1__3__1y), ._3__A3(n7408_4__6__2y), ._4__B3(n7408_4__6__2y), ._5__Vcc(1'b1),
    ._7__B2(n7408_4__6__2y), ._8__A2(n7408_4__6__2y), ._16__B4(n7432_2__3__1y), ._15__S4(F3), ._14__Cout(C),
    ._13__Cin(n7408_4__6__2y), ._12__GND(1'b0), ._11__B1(n7408_4__6__2y), ._10__A1(n7408_4__6__2y));  // open: _2__S3, _6__S2, _9__S1
  _7483 u_7483_2 (
    ._1__A4(n7432_1__6__2y), ._3__A3(n7408_4__11__4y), ._4__B3(n7408_4__11__4y), ._5__Vcc(1'b1),
    ._7__B2(n7408_4__11__4y), ._8__A2(n7408_4__11__4y), ._16__B4(n7432_2__6__2y), ._15__S4(F2),
    ._14__Cout(n7483_2__14__cout), ._13__Cin(n7408_4__11__4y), ._12__GND(1'b0), ._11__B1(n7408_4__11__4y),
    ._10__A1(n7408_4__11__4y));  // open: _2__S3, _6__S2, _9__S1
  _7483 u_7483_3 (
    ._1__A4(n7432_1__11__4y), ._3__A3(n7408_4__8__3y), ._4__B3(n7408_4__8__3y), ._5__Vcc(1'b1),
    ._7__B2(n7408_4__8__3y), ._8__A2(n7408_4__8__3y), ._16__B4(n7432_2__11__4y), ._15__S4(F1),
    ._14__Cout(n7483_3__14__cout), ._13__Cin(n7408_4__8__3y), ._12__GND(1'b0), ._11__B1(n7408_4__8__3y),
    ._10__A1(n7408_4__8__3y));  // open: _2__S3, _6__S2, _9__S1
  _7483 u_7483_4 (
    ._1__A4(n7432_2__8__3y), ._3__A3(n7408_4__3__1y), ._4__B3(n7408_4__3__1y), ._5__Vcc(1'b1),
    ._7__B2(n7408_4__3__1y), ._8__A2(n7408_4__3__1y), ._16__B4(n7432_1__8__3y), ._15__S4(F0),
    ._14__Cout(n7483_4__14__cout), ._13__Cin(n7408_4__3__1y), ._12__GND(1'b0), ._11__B1(n7408_4__3__1y),
    ._10__A1(n7408_4__3__1y));  // open: _2__S3, _6__S2, _9__S1
  _7408 u_7408_4 (
    ._1__1A(n7404_1__10__5y), ._2__1B(cs1), ._3__1Y(n7408_4__3__1y), ._4__2A(n7404_1__10__5y),
    ._5__2B(n7483_2__14__cout), ._6__2Y(n7408_4__6__2y), ._7__GND(1'b0), ._14__Vcc(1'b1),
    ._13__4B(n7404_1__10__5y), ._12__4A(n7483_3__14__cout), ._11__4Y(n7408_4__11__4y),
    ._10__3B(n7404_1__10__5y), ._9__3A(n7483_4__14__cout), ._8__3Y(n7408_4__8__3y));
  // _7432 7432_3: pin names not known; wires that end beside it: n7483_2__14__cout, n7432_3_p2, n7432_3_p3, n7432_3_p4, 1'b0, 1'b1, F0, F1, n7432_3_p2, F2, F3, n7432_3_p3
  // _7486 7486_1: pin names not known; wires that end beside it: n7404_1__10__5y, n7483_2__14__cout, C, n7483_2__14__cout, C, V, 1'b0, 1'b1, in_1, n7432_3_p4, Z, F3, F2, F1, F0

  assign S = F3;

  // Notes on the sheet:
  //   s0s2Bi'
  //   s0' Bi
  //   s2Bi'
  //   Xi
  //   Yi
endmodule
