// Logisim project Offline2.circ as structural Verilog: 12 circuits, main circuit main
module main (
  input  [31:0] A,
  input  [31:0] B,
  output [27:0] out_3,
  output [27:0] out_4,
  output out_5,
  output [31:0] Output,
  output Overflow,
  output UnderFlow
);

  wire comparator_1_x____y, normalize_1_allzero, rounding_1_shift, subtractor_1_bout;
  wire [4:0] normalize_1_shifts, shifterprep_1_out_2;
  wire [9:0] comparator_1_diff, comparator_1_larger;
  wire [10:0] add2_1_out_2, bit_extender_1_out, bit_extender_2_out, subtractor_1_out;
  wire [10:10] adder_1_out;
  wire [23:0] n2_s_complement_1_out_3, n2_s_complement_2_out_3;
  wire [24:0] normalize_1_normalizedout;
  wire [27:0] extender_1_out_2, mux_1_p1, mux_2_p5, shifter_1_out, signdetect_1_out_3;

  Comparator comparator_1 (
    .in_1(A[30:21]), .in_2(B[30:21]), .X____Y(comparator_1_x____y), .DIFF(comparator_1_diff),
    .LARGER(comparator_1_larger));
  ShifterPrep shifterprep_1 (.in_1(comparator_1_diff), .out_2(shifterprep_1_out_2));
  Add2 add2_1 (.in_1(comparator_1_larger), .out_2(add2_1_out_2));
  Adder #(.width(11)) adder_1 (
    .a(subtractor_1_out), .b(bit_extender_1_out), .out({adder_1_out[10], Output[30:21]}), .cin(1'b0));  // open: cout
  assign bit_extender_1_out = {{10{1'b0}}, rounding_1_shift};  // Bit_Extender bit_extender_1
  _2_s_Complement u_2_s_complement_1 (.in_1({3'b001, A[20:0]}), .in_2(A[31]), .out_3(n2_s_complement_1_out_3));
  Subtractor #(.width(11)) subtractor_1 (
    .a(add2_1_out_2), .b(bit_extender_2_out), .out(subtractor_1_out), .bin(1'b0), .bout(subtractor_1_bout));
  Flags flags_1 (
    .Exponent(Output[30:21]), .AllZeros(normalize_1_allzero), .Borrow(subtractor_1_bout),
    .Exponent10(adder_1_out[10]), .Overflow(Overflow), .Underflow(UnderFlow));
  extender extender_1 (.in_1(n2_s_complement_1_out_3), .out_2(extender_1_out_2));
  // Mux mux_1: pin names not known; wires that end beside it: mux_1_p1, extender_1_out_2, out_3, comparator_1_x____y
  Shifter #(.width(28), .shift("ar")) shifter_1 (.in(out_3), .\dist (shifterprep_1_out_2), .out(shifter_1_out));
  assign bit_extender_2_out = {{6{1'b0}}, normalize_1_shifts};  // Bit_Extender bit_extender_2
  Rounding rounding_1 (.in_1(normalize_1_normalizedout), .Fraction(Output[20:0]), .Shift(rounding_1_shift));
  // Mux mux_2: pin names not known; wires that end beside it: extender_1_out_2, mux_1_p1, out_4, comparator_1_x____y, mux_2_p5
  SignDetect signdetect_1 (.in_1(mux_2_p5), .out_2(out_5), .out_3(signdetect_1_out_3));
  Normalize normalize_1 (
    .in_1(signdetect_1_out_3), .Shifts(normalize_1_shifts), .NormalizedOut(normalize_1_normalizedout),
    .AllZero(normalize_1_allzero));
  Adder #(.width(28)) adder_2 (.a(out_4), .b(shifter_1_out), .out(mux_2_p5), .cin(1'b0));  // open: cout
  _2_s_Complement u_2_s_complement_2 (.in_1({3'b001, B[20:0]}), .in_2(B[31]), .out_3(n2_s_complement_2_out_3));
  extender extender_2 (.in_1(n2_s_complement_2_out_3), .out_2(mux_1_p1));

  assign Output[31] = out_5;

  // Notes on the sheet:
  //   Comparator
  //   ShifterPrep
  //   Add2
  //   Extender
  //   2's Comp
  //   Mux
  //   Shifter
  //   Flags
  //   Round
  //   Smaller
  //   Mux
  //   SignDetect
  //   Normalize
  //   2's Comp
  //   Larger
  //   Extender
endmodule

module Comparator (
  input  [9:0] in_1,
  input  [9:0] in_2,
  output X____Y,
  output [9:0] DIFF,
  output [9:0] LARGER
);

  wire comparator_1_eq, comparator_1_gt, comparator_1_lt;
  wire [9:0] multiplexer_1_out;

  Multiplexer #(.width(10), .disabled(0), .enable("false")) multiplexer_1 (
    .in0(in_1), .in1(in_2), .out(multiplexer_1_out), .sel(comparator_1_gt));
  Multiplexer #(.width(10), .disabled(0), .enable("false")) multiplexer_2 (
    .in0(in_1), .in1(in_2), .out(LARGER), .sel(comparator_1_lt));
  Comparator_part #(.width(10), .mode("unsigned")) comparator_1 (
    .a(in_1), .b(in_2), .gt(comparator_1_gt), .eq(comparator_1_eq), .lt(comparator_1_lt));
  Subtractor #(.width(10)) subtractor_1 (.a(LARGER), .b(multiplexer_1_out), .out(DIFF), .bin(1'b0));  // open: bout
  or or_1 (X____Y, comparator_1_gt, comparator_1_eq);
endmodule

module _2_s_Complement (
  input  [23:0] in_1,
  input  in_2,
  output [23:0] out_3
);

  wire [23:0] negator_1_out;

  Negator #(.width(24)) negator_1 (.in(in_1), .out(negator_1_out));
  Multiplexer #(.width(24), .disabled(0), .enable("false")) multiplexer_1 (
    .in0(in_1), .in1(negator_1_out), .out(out_3), .sel(in_2));
endmodule

module ShifterPrep (
  input  [9:0] in_1,
  output [4:0] out_2
);

  wire n7432_1_p3, n7432_1_p6, n7432_1_p11, n7432_1_p14;

  // _7432 7432_1: pin names not known; wires that end beside it: in_1[8], in_1[9], n7432_1_p3, n7432_1_p3, in_1[7], n7432_1_p6, 1'b0, 1'b1, in_1[6], n7432_1_p6, n7432_1_p11, n7432_1_p11, in_1[5], n7432_1_p14
  // _7432 7432_2: pin names not known; wires that end beside it: in_1[4], n7432_1_p14, out_2[4], 1'b0, 1'b1, in_1[3], n7432_1_p14, out_2[3], in_1[2], n7432_1_p14, out_2[2]

  assign out_2[1:0] = in_1[1:0];
endmodule

module SignDetect (
  input  [27:0] in_1,
  output out_2,
  output [27:0] out_3
);

  wire [27:0] negator_1_out;

  Negator #(.width(28)) negator_1 (.in(in_1), .out(negator_1_out));
  // Mux mux_1: pin names not known; wires that end beside it: in_1[27], out_3, in_1, negator_1_out

  assign out_2 = in_1[27];
endmodule

module Normalize (
  input  [27:0] in_1,
  output [4:0] Shifts,
  output [24:0] NormalizedOut,
  output AllZero
);

  wire bitfinder_1_found;
  wire [27:0] n7404_1_p5;

  BitFinder #(.width(28)) bitfinder_1 (
    .in({in_1[0], in_1[1], in_1[2], in_1[3], in_1[4], in_1[5], in_1[6], in_1[7], in_1[8], in_1[9], in_1[10], in_1[11], in_1[12], in_1[13], in_1[14], in_1[15], in_1[16], in_1[17], in_1[18], in_1[19], in_1[20], in_1[21], in_1[22], in_1[23], in_1[24], in_1[25], in_1[26], 1'b0}),
    .index(Shifts), .found(bitfinder_1_found));
  // _7404 7404_1: pin names not known; wires that end beside it: bitfinder_1_found, AllZero, 1'b0, 1'b1, n7404_1_p5[0], n7404_1_p5[1], n7404_1_p5[27]
  Shifter #(.width(28)) shifter_1 (.in(in_1), .\dist (Shifts), .out({n7404_1_p5[27], NormalizedOut, n7404_1_p5[1:0]}));
endmodule

module Add2 (
  input  [9:0] in_1,
  output [10:0] out_2
);

  Adder #(.width(11)) adder_1 (.a(11'h2), .b({1'b0, in_1}), .out(out_2), .cin(1'b0));  // open: cout
endmodule

module Flags (
  input  [9:0] Exponent,
  input  AllZeros,
  input  Borrow,
  input  Exponent10,
  output Overflow,
  output Underflow
);

  wire n7404_1_p1, n7404_1_p2, n7404_1_p4, n7408_1_p3, n7408_1_p6, n7408_1_p8, n7408_1_p9, n7408_2_p3,
       n7408_2_p6, n7408_2_p8, n7408_2_p9, n7408_3_p3, n7408_3_p6, n7432_1_p3, n7432_1_p6, n7432_1_p8,
       n7432_1_p9, n7432_2_p3, n7432_2_p6, n7432_2_p8, n7432_2_p9, n7432_4_p6;

  // _7432 7432_1: pin names not known; wires that end beside it: Exponent[9], Exponent[8], n7432_1_p3, n7432_1_p3, Exponent[7], n7432_1_p6, Exponent[5], n7432_1_p8, n7432_1_p9, Exponent[6], n7432_1_p6, n7432_1_p8
  // _7408 7408_1: pin names not known; wires that end beside it: Exponent[9], Exponent[8], n7408_1_p3, n7408_1_p3, Exponent[7], n7408_1_p6, Exponent[5], n7408_1_p8, n7408_1_p9, Exponent[6], n7408_1_p6, n7408_1_p8
  // _7432 7432_2: pin names not known; wires that end beside it: n7432_1_p9, Exponent[4], n7432_2_p3, n7432_2_p3, Exponent[3], n7432_2_p6, Exponent[1], n7432_2_p8, n7432_2_p9, Exponent[2], n7432_2_p6, n7432_2_p8
  // _7404 7404_1: pin names not known; wires that end beside it: n7404_1_p1, n7404_1_p2, Exponent10, n7404_1_p4
  // _7408 7408_2: pin names not known; wires that end beside it: Exponent[4], n7408_1_p9, n7408_2_p3, n7408_2_p3, Exponent[3], n7408_2_p6, Exponent[1], n7408_2_p8, n7408_2_p9, Exponent[2], n7408_2_p6, n7408_2_p8
  // _7432 7432_3: pin names not known; wires that end beside it: n7432_2_p9, Exponent[0], n7404_1_p1
  // _7408 7408_3: pin names not known; wires that end beside it: Exponent[0], n7408_2_p9, n7408_3_p3, n7404_1_p4, n7404_1_p2, n7408_3_p6
  // _7432 7432_4: pin names not known; wires that end beside it: Exponent10, n7408_3_p3, Overflow, n7408_3_p6, AllZeros, n7432_4_p6, n7432_4_p6, Borrow, Underflow

  // Notes on the sheet:
  //   NOR_BITS
endmodule

module extender (
  input  [23:0] in_1,
  output [27:0] out_2
);


  assign out_2 = {in_1, 4'b0000};
endmodule

module Rounding (
  input  [24:0] in_1,
  output [20:0] Fraction,
  output Shift
);

  wire n7432_1_p3, n7432_1_p6, n7432_1_p9;
  wire [0:0] n7408_1_p3;
  wire [4:0] bit_extender_1_out;
  wire [21:0] adder_1_out;
  wire [22:21] shifter_1_out;

  // _7432 7432_1: pin names not known; wires that end beside it: in_1[1], in_1[0], n7432_1_p3, n7432_1_p3, in_1[2], n7432_1_p6, in_1[4], n7432_1_p6, n7432_1_p9
  // _7408 7408_1: pin names not known; wires that end beside it: in_1[3], n7432_1_p9, n7408_1_p3[0]
  Adder #(.width(23)) adder_1 (
    .a({2'b01, in_1[24:4]}), .b({{22{1'b0}}, n7408_1_p3[0]}), .out({Shift, adder_1_out}), .cin(1'b0));  // open: cout
  assign bit_extender_1_out = {{4{1'b0}}, Shift};  // Bit_Extender bit_extender_1
  Shifter #(.width(23), .shift("lr")) shifter_1 (
    .in({Shift, adder_1_out}), .\dist (bit_extender_1_out), .out({shifter_1_out, Fraction}));

  // Notes on the sheet:
  //   S
  //   R
endmodule

module FPA (
  input  [31:0] A,
  input  [31:0] B,
  output Overlfow,
  output Underflow,
  output [31:0] Result
);

  wire n7404_1_p3, n7404_1_p4, n7404_1_p5, n7404_1_p6, n7404_1_p7, n7404_1_p8;
  wire [1:0] n7408_1_p7;
  wire [31:0] main_1_output;
  wire [31:31] n7404_1_p2;

  main main_1 (
    .A(A), .B(B), .Overflow(Overlfow), .UnderFlow(Underflow), .Output(main_1_output));  // open: out_3, out_4, out_5
  // _7404 7404_1: pin names not known; wires that end beside it: A[31], n7404_1_p2[31], n7404_1_p3, n7404_1_p4, n7404_1_p5, n7404_1_p6, n7404_1_p7, n7404_1_p8
  Multiplexer #(.select(2), .width(32), .enable("false")) multiplexer_1 (
    .in0({32{1'b0}}), .in1(A), .in2(B), .in3(main_1_output), .out(Result), .sel(n7408_1_p7));
  Comparator_part #(.width(32)) comparator_1 (.a({n7404_1_p2[31], A[30:0]}), .b(B), .eq(n7404_1_p3));  // open: gt, lt
  Comparator_part #(.width(32)) comparator_2 (.a(A), .b({32{1'b0}}), .eq(n7404_1_p7));  // open: gt, lt
  Comparator_part #(.width(32)) comparator_3 (.a(B), .b({32{1'b0}}), .eq(n7404_1_p5));  // open: gt, lt
  // _7408 7408_1: pin names not known; wires that end beside it: n7404_1_p7, n7404_1_p4, n7404_1_p6, n7408_1_p7[1], n7404_1_p8, n7404_1_p4, n7408_1_p7[0], n7404_1_p5

  // Notes on the sheet:
  //   P'
  //   P
  //   P'R'
  //   Q'
  //   Q
  //   R
  //   R'
endmodule

module Final_Circuit (
  input  [31:0] in_1,
  input  [31:0] in_2,
  output [31:0] out_3,
  output out_4,
  output out_5
);

  FPA fpa_1 (.A(in_1), .B(in_2), .Overlfow(out_4), .Underflow(out_5), .Result(out_3));

  // Notes on the sheet:
  //   A
  //   B
  //   Floating point adder
  //   Overflow
  //   Underflow
endmodule
