// Logisim project ALU.circ as structural Verilog: 1 circuit, main circuit ALU
module ALU (
  input  [3:0] A,
  input  [3:0] B,
  input  [2:0] OPcode,
  output Overflow,
  output Zflag,
  output Negative,
  output [3:0] Output
);

  wire [3:0] adder_1_out, and_1_out, not_1_out, or_1_out, shifter_1_out, shifter_2_out, subtractor_1_out,
       undriven;

  Adder #(.width(4)) adder_1 (.a(A), .b(B), .out(adder_1_out), .cin(1'b0), .cout(Overflow));
  Subtractor #(.width(4)) subtractor_1 (.a(A), .b(B), .out(subtractor_1_out), .bin(1'b0), .bout(Negative));
  assign and_1_out = A & B;  // AND_Gate and_1, 4 bits wide
  assign or_1_out = A | B;  // OR_Gate or_1, 4 bits wide
  Shifter #(.width(4)) shifter_1 (.in(A), .\dist (B[1:0]), .out(shifter_1_out));
  Shifter #(.width(4), .shift("lr")) shifter_2 (.in(A), .\dist (B[1:0]), .out(shifter_2_out));
  assign not_1_out = ~or_1_out;  // NOT_Gate not_1, 4 bits wide
  Multiplexer #(.select(3), .width(4), .enable("false")) multiplexer_1 (
    .in0(adder_1_out), .in1(shifter_1_out), .in2(subtractor_1_out), .in3(or_1_out), .in4(and_1_out),
    .in5(shifter_2_out), .in6(not_1_out), .in7(undriven), .out(Output), .sel(OPcode));
  nor nor_1 (Zflag, Output[0], Output[1], Output[2], Output[3]);
endmodule
