// Logisim project ControlUnit.circ as structural Verilog: 1 circuit, main circuit ControlUnit
module ControlUnit (
  input  [3:0] OPCODE,
  output MemToReg,
  output [2:0] ALUOP,
  output AluSrc,
  output BNEQ,
  output BEQ,
  output Jump,
  output MemRead,
  output MemWrite,
  output RegWrite,
  output RegDist
);

  ROM #(.addrWidth(4), .dataWidth(12)) rom_1 (
    .addr(OPCODE), .data({RegDist, RegWrite, MemWrite, MemRead, Jump, BEQ, BNEQ, AluSrc, ALUOP, MemToReg}),
    .sel(1'b1));

  // Notes on the sheet:
  //   contents of rom_1 (hex, n*v repeats v):
  //   c00 412 24 416 210 c06 80 c04 418 c08 511 414 410 44 41a c0c
endmodule
