// Logisim project DataMemory.circ as structural Verilog: 1 circuit, main circuit DataMemory
// DM
module DataMemory (
  input  [3:0] Address,
  input  MemWrite,
  input  [3:0] WriteData,
  input  CLK,
  input  MemRead,
  output [3:0] ReadData
);

  RAM #(.addrWidth(4), .dataWidth(4), .bus("separate")) ram_1 (
    .addr(Address), .din(WriteData), .data(ReadData), .str(MemWrite), .sel(1'b1), .clk(CLK), .ld(MemRead),
    .clr(1'b0));
endmodule
