// Logisim project RegisterFile.circ as structural Verilog: 1 circuit, main circuit RegisterFile
module RegisterFile (
  input  WriteEnable,
  input  [3:0] ReadRegister1,
  input  [3:0] ReadRegister2,
  input  [3:0] WriteRegister,
  input  [3:0] WriteData,
  input  CLK,
  output [3:0] zero,
  output [3:0] t0,
  output [3:0] t1,
  output [3:0] t2,
  output [3:0] t3,
  output [3:0] t4,
  output [3:0] t5,
  output [3:0] sp,
  output [3:0] ReadData1,
  output [3:0] ReadData2
);

  wire and_1_out, and_2_out, and_3_out, and_4_out, and_5_out, and_6_out, and_7_out, decoder_1_out1,
       decoder_1_out2, decoder_1_out3, decoder_1_out4, decoder_1_out5, decoder_1_out6, decoder_1_out7,
       undriven_2;
  wire [3:0] undriven;

  and and_1 (and_1_out, WriteEnable, decoder_1_out1);
  Register #(.width(4)) u_zero (.D(undriven), .en(undriven_2), .Q(zero), .clk(CLK));  // open: clr
  and and_2 (and_2_out, WriteEnable, decoder_1_out2);
  Register #(.width(4)) u_t0 (.D(WriteData), .en(and_1_out), .Q(t0), .clk(CLK));  // open: clr
  Multiplexer #(.select(3), .width(4), .enable("false")) multiplexer_1 (
    .in0(zero), .in1(t0), .in2(t1), .in3(t2), .in4(t3), .in5(t4), .in6(t5), .in7(sp), .out(ReadData1),
    .sel(ReadRegister1[2:0]));
  and and_3 (and_3_out, WriteEnable, decoder_1_out3);
  Register #(.width(4)) u_t1 (.D(WriteData), .en(and_2_out), .Q(t1), .clk(CLK));  // open: clr
  and and_4 (and_4_out, WriteEnable, decoder_1_out4);
  Register #(.width(4)) u_t2 (.D(WriteData), .en(and_3_out), .Q(t2), .clk(CLK));  // open: clr
  and and_5 (and_5_out, WriteEnable, decoder_1_out5);
  Register #(.width(4)) u_t3 (.D(WriteData), .en(and_4_out), .Q(t3), .clk(CLK));  // open: clr
  Multiplexer #(.select(3), .width(4), .enable("false")) multiplexer_2 (
    .in0(zero), .in1(t0), .in2(t1), .in3(t2), .in4(t3), .in5(t4), .in6(t5), .in7(sp), .out(ReadData2),
    .sel(ReadRegister2[2:0]));
  and and_6 (and_6_out, WriteEnable, decoder_1_out6);
  Register #(.width(4)) u_t4 (.D(WriteData), .en(and_5_out), .Q(t4), .clk(CLK));  // open: clr
  Decoder #(.select(3), .enable("false")) decoder_1 (
    .out1(decoder_1_out1), .out2(decoder_1_out2), .out3(decoder_1_out3), .out4(decoder_1_out4),
    .out5(decoder_1_out5), .out6(decoder_1_out6), .out7(decoder_1_out7), .sel(WriteRegister[2:0]));  // open: out0
  and and_7 (and_7_out, WriteEnable, decoder_1_out7);
  Register #(.width(4)) u_t5 (.D(WriteData), .en(and_6_out), .Q(t5), .clk(CLK));  // open: clr
  Register #(.width(4)) u_sp (.D(WriteData), .en(and_7_out), .Q(sp), .clk(CLK));  // open: clr
endmodule
