// Logisim project main.circ as structural Verilog: 1 circuit, main circuit main
module main (
  output [1:0] out_1,
  output [3:0] OPCODE,
  output [15:0] out_3,
  output out_4,
  output [7:0] JUMP,
  output [3:0] zero,
  output [3:0] t0,
  output [3:0] t1,
  output [3:0] t2,
  output [3:0] t3,
  output [3:0] t4,
  output [3:0] t5,
  output [3:0] sp
);

  wire and_1_out, and_2_out, clock_1_out, controlunit_1_alusrc, controlunit_1_beq, controlunit_1_bneq,
       controlunit_1_jump, controlunit_1_memread, controlunit_1_memtoreg, controlunit_1_memwrite,
       controlunit_1_regdist, controlunit_1_regwrite, not_1_out;
  wire [2:0] controlunit_1_aluop;
  wire [3:0] alu_1_output, datamemory_1_readdata, multiplexer_1_out, multiplexer_3_out, multiplexer_4_out,
       registerfile_1_readdata1, registerfile_1_readdata2;
  wire [7:0] adder_1_out, adder_2_out, bit_extender_1_out, multiplexer_2_out, PC_q;

  Clock clock_1 (.out(clock_1_out));
  Register PC (.D(multiplexer_2_out), .en(1'b1), .Q(PC_q), .clk(clock_1_out));  // open: clr
  Adder adder_1 (.a(PC_q), .b(8'h1), .out(adder_1_out), .cin(1'b0));  // open: cout
  ROM #(.dataWidth(16)) rom_1 (.addr(PC_q), .data({OPCODE, JUMP, out_3[3:0]}), .sel(1'b1));
  assign bit_extender_1_out = {{4{1'b0}}, out_3[3:0]};  // Bit_Extender bit_extender_1
  ControlUnit controlunit_1 (
    .OPCODE(OPCODE), .MemToReg(controlunit_1_memtoreg), .ALUOP(controlunit_1_aluop),
    .AluSrc(controlunit_1_alusrc), .BNEQ(controlunit_1_bneq), .BEQ(controlunit_1_beq),
    .Jump(controlunit_1_jump), .MemRead(controlunit_1_memread), .MemWrite(controlunit_1_memwrite),
    .RegWrite(controlunit_1_regwrite), .RegDist(controlunit_1_regdist));
  Adder adder_2 (.a(adder_1_out), .b(bit_extender_1_out), .out(adder_2_out));  // open: cin, cout
  Multiplexer #(.width(4), .enable("false")) multiplexer_1 (
    .in0(JUMP[3:0]), .in1(out_3[3:0]), .out(multiplexer_1_out), .sel(controlunit_1_regdist));
  and and_1 (and_1_out, controlunit_1_bneq, not_1_out);
  Multiplexer #(.select(2), .width(8), .enable("false")) multiplexer_2 (
    .in0(adder_1_out), .in1(JUMP), .in2(adder_2_out), .in3(adder_2_out), .out(multiplexer_2_out), .sel(out_1));
  Priority_Encoder #(.select(2)) priority_encoder_1 (
    .in0(1'b1), .in1(controlunit_1_jump), .in2(and_1_out), .in3(and_2_out), .out(out_1));
  not not_1 (not_1_out, out_4);
  RegisterFile registerfile_1 (
    .ReadRegister1(JUMP[7:4]), .ReadRegister2(JUMP[3:0]), .WriteRegister(multiplexer_1_out),
    .WriteData(multiplexer_4_out), .WriteEnable(controlunit_1_regwrite), .CLK(clock_1_out), .zero(zero),
    .t0(t0), .t1(t1), .t2(t2), .t3(t3), .t4(t4), .t5(t5), .sp(sp), .ReadData1(registerfile_1_readdata1),
    .ReadData2(registerfile_1_readdata2));
  and and_2 (and_2_out, controlunit_1_beq, out_4);
  ALU alu_1 (
    .A(registerfile_1_readdata1), .B(multiplexer_3_out), .OPcode(controlunit_1_aluop), .Zflag(out_4),
    .Output(alu_1_output));  // open: Overflow, Negative
  Multiplexer #(.width(4), .enable("false")) multiplexer_3 (
    .in0(registerfile_1_readdata2), .in1(out_3[3:0]), .out(multiplexer_3_out), .sel(controlunit_1_alusrc));
  DataMemory datamemory_1 (
    .Address(alu_1_output), .WriteData(registerfile_1_readdata2), .MemRead(controlunit_1_memread),
    .MemWrite(controlunit_1_memwrite), .CLK(clock_1_out), .ReadData(datamemory_1_readdata));
  Multiplexer #(.width(4), .enable("false")) multiplexer_4 (
    .in0(alu_1_output), .in1(datamemory_1_readdata), .out(multiplexer_4_out), .sel(controlunit_1_memtoreg));

  assign out_3[15:4] = {OPCODE, JUMP};

  // Notes on the sheet:
  //   contents of rom_1 (hex, n*v repeats v):
  //   c027 c228 b221 4200 a300 4020 a030
endmodule
