// Logisim project register_file.circ as structural Verilog: 1 circuit, main circuit main
module main (
  input  WriteEnable,
  input  [3:0] WriteRegister,
  input  [7:0] WriteData,
  input  [3:0] ReadRegister1,
  input  [7:0] ReadData1,
  input  in_6,
  input  [7:0] ReadData2,
  input  [3:0] ReadRegister2,
  input  [7:0] in_9,
  input  in_10,
  output [7:0] out_11
);

  wire and_1_out, and_2_out, and_3_out, and_4_out, and_5_out, and_6_out, and_7_out, clock_1_out, clock_2_out,
       decoder_1_out1, decoder_1_out2, decoder_1_out3, decoder_1_out4, decoder_1_out5, decoder_1_out6,
       decoder_1_out7, undriven_2;
  wire [7:0] sp_q, t0_q, t1_q, t2_q, t3_q, t4_q, t5_q, undriven, zero_q;

  Clock clock_1 (.out(clock_1_out));
  and and_1 (and_1_out, WriteEnable, decoder_1_out1);
  Register zero (.D(undriven), .en(undriven_2), .Q(zero_q), .clk(clock_1_out));  // open: clr
  and and_2 (and_2_out, WriteEnable, decoder_1_out2);
  Register t0 (.D(WriteData), .en(and_1_out), .Q(t0_q), .clk(clock_1_out));  // open: clr
  Multiplexer #(.select(3), .width(8)) multiplexer_1 (
    .in0(zero_q), .in1(t0_q), .in2(t1_q), .in3(t2_q), .in4(t3_q), .in5(t4_q), .in6(t5_q), .in7(sp_q),
    .out(ReadData1), .sel(ReadRegister1[2:0]), .en(in_6));
  and and_3 (and_3_out, WriteEnable, decoder_1_out3);
  Register t1 (.D(WriteData), .en(and_2_out), .Q(t1_q), .clk(clock_1_out));  // open: clr
  and and_4 (and_4_out, WriteEnable, decoder_1_out4);
  Register t2 (.D(WriteData), .en(and_3_out), .Q(t2_q), .clk(clock_1_out));  // open: clr
  Clock clock_2 (.out(clock_2_out));
  and and_5 (and_5_out, WriteEnable, decoder_1_out5);
  Register t3 (.D(WriteData), .en(and_4_out), .Q(t3_q), .clk(clock_1_out));  // open: clr
  Multiplexer #(.select(3), .width(8)) multiplexer_2 (
    .in0(zero_q), .in1(t0_q), .in2(t1_q), .in3(t2_q), .in4(t3_q), .in5(t4_q), .in6(t5_q), .in7(sp_q),
    .out(ReadData2), .sel(ReadRegister2[2:0]), .en(in_6));
  and and_6 (and_6_out, WriteEnable, decoder_1_out6);
  Register t4 (.D(WriteData), .en(and_5_out), .Q(t4_q), .clk(clock_1_out));  // open: clr
  Decoder #(.select(3)) decoder_1 (
    .out1(decoder_1_out1), .out2(decoder_1_out2), .out3(decoder_1_out3), .out4(decoder_1_out4),
    .out5(decoder_1_out5), .out6(decoder_1_out6), .out7(decoder_1_out7), .sel(WriteRegister[2:0]), .en(in_6));  // open: out0
  and and_7 (and_7_out, WriteEnable, decoder_1_out7);
  Register t5 (.D(WriteData), .en(and_6_out), .Q(t5_q), .clk(clock_1_out));  // open: clr
  Register sp (.D(WriteData), .en(and_7_out), .Q(sp_q), .clk(clock_1_out));  // open: clr
  Register register_1 (.D(in_9), .en(in_10), .Q(out_11), .clk(clock_2_out));  // open: clr
endmodule
