// Logisim project memory_chips_practice.circ as structural Verilog: 1 circuit, main circuit main
module main (
  input  [7:0] Address,
  input  [7:0] Input_data,
  input  in_3,
  input  in_4,
  output [7:0] Data_Output,
  output [7:0] ROM_Output
);

  wire clock_1_out, not_1_out;

  not not_1 (not_1_out, in_4);
  RAM #(.bus("separate")) ram_1 (
    .addr(Address), .din(Input_data), .data(Data_Output), .str(not_1_out), .sel(in_3), .clk(clock_1_out),
    .ld(in_4));  // open: clr
  ROM rom_1 (.addr(Address), .data(ROM_Output), .sel(in_3));
  Clock clock_1 (.out(clock_1_out));

  // Notes on the sheet:
  //   contents of rom_1 (hex, n*v repeats v):
  //   32 23 0 23 0 0 0 4 0 4 0 0 2 6 7 89 5 0 32 67*0 cc 0 0 0 f
endmodule
